// Logisim project main_cpu.circ as structural Verilog: 1 circuit, main circuit main
module main (
);

  wire and_2_out, and_3_out, and_4_out, and_5_out, and_6_out, and_7_out, and_14_out, andb0_src_in0,
       andb0_src_in1, clock_1_out, demultiplexer_1_out0, demultiplexer_1_out1, demultiplexer_1_out2,
       demultiplexer_1_out3, destsel_b0, destsel_b0_out, destsel_b1, destsel_b1_out, isart_en, moven,
       n74193_1_pin4, n74193_1_pin12, n74193_2_pin1, n74193_2_pin4, not_1_out, not_2_out, not_3_out,
       not_4_out, not_5_out, not_6_out, not_7_out, not_8_out, not_10_out, or_5_out;
  wire [0:0] and_9_out;
  wire [1:0] demultiplexer_3_out0, demultiplexer_3_out1, n74193_2_pin3, n74193_2_pin6, register_3_q,
       register_3_q_3;
  wire [2:0] and_13_out;
  wire [5:3] register_3_q_2;
  wire [7:0] adder_1_out, and_10_out, demultiplexer_2_out0, demultiplexer_2_out1, demultiplexer_2_out2,
       demultiplexer_2_out3, divider_1_out, divider_1_rem, multiplexer_1_out, multiplexer_2_out,
       multiplexer_3_out, multiplier_1_out, n74193_1_pin3, or_3_out, register_1_q, register_2_q,
       register_4_q, register_5_q, rom_1_data, subtractor_1_out, xor_1_out;

  and and_1 (destsel_b0, andb0_src_in0, andb0_src_in1);
  or or_1 (destsel_b0_out, and_2_out, destsel_b0);
  or or_2 (destsel_b1_out, and_3_out, destsel_b1);
  and and_2 (and_2_out, isart_en, register_3_q_3[0]);
  and and_3 (and_3_out, isart_en, register_3_q_3[1]);
  ROM rom_1 (.addr(n74193_1_pin3), .data(rom_1_data));
  Clock clock_1 (.out(clock_1_out));
  and and_4 (and_4_out, clock_1_out, not_1_out);
  not not_1 (not_1_out, and_5_out);
  not not_2 (not_2_out, register_3_q_3[0]);
  not not_3 (not_3_out, register_3_q_2[5]);
  not not_4 (not_4_out, register_3_q_2[4]);
  and and_5 (and_5_out, register_3_q_3[1], not_2_out, not_3_out, not_4_out, not_5_out, not_6_out, not_7_out, not_8_out);
  not not_5 (not_5_out, register_3_q_2[3]);
  not not_6 (not_6_out, andb0_src_in0);
  not not_7 (not_7_out, register_3_q[1]);
  not not_8 (not_8_out, register_3_q[0]);
  Register register_1 (.D(demultiplexer_2_out1), .clk(and_6_out), .Q(register_1_q));  // open: en, clr
  and and_6 (and_6_out, and_4_out, demultiplexer_1_out1);
  Register register_2 (.D(demultiplexer_2_out0), .clk(and_7_out), .Q(register_2_q));  // open: en, clr
  and and_7 (and_7_out, demultiplexer_1_out0, and_4_out);
  and and_8 (destsel_b1, register_3_q[1], andb0_src_in1);
  and and_9 (and_9_out[0], register_3_q[0], andb0_src_in1);
  Register register_3 (
    .D(rom_1_data), .clk(and_4_out), .Q({register_3_q_3, register_3_q_2, andb0_src_in0, register_3_q}));  // open: en, clr
  // Probe on rom_1_data
  Adder adder_1 (.a(register_1_q), .b(register_2_q), .out(adder_1_out));  // open: cin, cout
  Subtractor subtractor_1 (.a(register_1_q), .b(register_2_q), .out(subtractor_1_out));  // open: bin, bout
  Multiplier multiplier_1 (.a(register_1_q), .b(register_2_q), .out(multiplier_1_out));  // open: cin, cout
  Divider divider_1 (.a(register_1_q), .b(register_2_q), .out(divider_1_out), .rem(divider_1_rem));  // open: upper
  assign and_10_out = register_1_q & register_2_q;  // AND_Gate and_10, 8 bits wide
  assign or_3_out = register_1_q | register_2_q;  // OR_Gate or_3, 8 bits wide
  assign xor_1_out = register_1_q ^ register_2_q;  // XOR_Gate xor_1, 8 bits wide
  not not_9 (andb0_src_in1, isart_en);
  nor nor_1 (isart_en, register_3_q_2[5], register_3_q_2[4], register_3_q_2[3]);
  and and_11 (and_13_out[2], isart_en, andb0_src_in0);
  not not_10 (not_10_out, and_4_out);
  and and_12 (and_13_out[1], isart_en, register_3_q[1]);
  and and_13 (and_13_out[0], isart_en, register_3_q[0]);
  _74193 u_74193_1 (
    .pin2(n74193_1_pin3[1]), .pin3(n74193_1_pin3[0]), .pin4(n74193_1_pin4), .pin5(and_4_out),
    .pin6(n74193_1_pin3[2]), .pin7(n74193_1_pin3[3]), .pin12(n74193_1_pin12));  // open: pin1, pin15, pin14, pin13, pin11, pin10, pin9
  // Probe on n74193_1_pin3
  Register register_4 (.D(demultiplexer_2_out2), .clk(and_14_out), .Q(register_4_q));  // open: en, clr
  and and_14 (and_14_out, and_4_out, demultiplexer_1_out2);
  Register register_5 (.D(multiplexer_1_out), .clk(and_4_out), .Q(register_5_q));  // open: en, clr
  // Probe on multiplexer_1_out
  Multiplexer #(.select(3), .width(8)) multiplexer_1 (
    .in0(adder_1_out), .in1(subtractor_1_out), .in2(multiplier_1_out), .in3(divider_1_out),
    .in4(divider_1_rem), .in5(and_10_out), .in6(or_3_out), .in7(xor_1_out), .out(multiplexer_1_out),
    .sel(and_13_out));
  _74193 u_74193_2 (
    .pin1(n74193_2_pin1), .pin2(n74193_2_pin3[1]), .pin3(n74193_2_pin3[0]), .pin4(n74193_2_pin4),
    .pin5(isart_en), .pin6(n74193_2_pin6[0]), .pin7(n74193_2_pin6[1]), .pin15(n74193_1_pin4),
    .pin11(not_10_out), .pin10(n74193_2_pin1), .pin9(n74193_2_pin1));  // open: pin14, pin13, pin12
  _74193 u_74193_3 (
    .pin2(n74193_1_pin3[5]), .pin3(n74193_1_pin3[4]), .pin4(n74193_1_pin4), .pin5(n74193_1_pin12),
    .pin6(n74193_1_pin3[6]), .pin7(n74193_1_pin3[7]));  // open: pin1, pin15, pin14, pin13, pin12, pin11, pin10, pin9
  RAM ram_1 (
    .addr(register_4_q), .we(register_3_q_2[3]), .oe(register_3_q_2[4]), .clk(and_4_out), .din(register_5_q),
    .dout(register_5_q));
  or or_4 (moven, register_3_q_2[5], isart_en);
  // Probe on register_5_q
  or or_5 (or_5_out, n74193_2_pin6[1], n74193_2_pin6[0], n74193_2_pin3[1], n74193_2_pin3[0]);
  and and_15 (n74193_2_pin4, or_5_out, and_4_out);
  Button #(.press("passive")) button_1 (.out(n74193_1_pin4));
  Multiplexer #(.enable("true"), .select(2), .width(8)) multiplexer_2 (
    .in0(register_2_q), .in1(register_1_q), .in2(register_4_q), .in3(register_5_q), .out(multiplexer_2_out),
    .sel(demultiplexer_3_out0), .en(moven));
  // AND_Gate and_16 has open pins: in0=demultiplexer_1_out3, in1=and_4_out, out=open
  // NOT_Gate not_11 has open pins: in=or_5_out, out=open
  Demultiplexer #(.enable("true"), .select(2)) demultiplexer_1 (
    .out0(demultiplexer_1_out0), .out1(demultiplexer_1_out1), .out2(demultiplexer_1_out2),
    .out3(demultiplexer_1_out3), .in(moven), .sel({destsel_b1_out, and_9_out[0]}), .en(moven));
  Demultiplexer #(.enable("true"), .select(2), .width(8)) demultiplexer_2 (
    .out0(demultiplexer_2_out0), .out1(demultiplexer_2_out1), .out2(demultiplexer_2_out2),
    .out3(demultiplexer_2_out3), .in(multiplexer_3_out), .sel({destsel_b1_out, and_9_out[0]}), .en(moven));
  Multiplexer #(.width(8)) multiplexer_3 (
    .in0(multiplexer_2_out), .in1({{6{1'b0}}, demultiplexer_3_out1}), .out(multiplexer_3_out),
    .sel(destsel_b0_out));
  Demultiplexer #(.width(2)) demultiplexer_3 (
    .out0(demultiplexer_3_out0), .out1(demultiplexer_3_out1), .in(register_3_q_3), .sel(destsel_b0_out));
  // Probe on register_5_q
  // also tied to GND on the sheet: n74193_2_pin1

  // Notes on the sheet:
  //   contents of rom_1 (hex, n*v repeats v):
  //   a5 0 e4 0 8 2 66 8 10 e1 0 a6 8 80 80
  //   ART [00] [0] [0] [0] [OP000]
  //   RAM [00MOV/SET VAL] [0MOV] [0LOAD] [0STORE] [0SET] [00MOV/SET LOC]
  //   000 ADD      00 REG B
  //   001 SUB       01 REG A
  //   010 MUL      10 MAR
  //   011 DIV       11 ACC
  //   100 MOD
  //   101 AND
  //   110 OR
  //   111 XOR
endmodule
